// Digital circuit Addr-Counter.dig as structural Verilog
module Addr_Counter (
  input  CLK,
  input  RUN,
  output [3:0] ADDR,
  output nPULSE
);

  wire counter_1_ovf, not_1_out, rs_ff_1_q;

  RS_FF rs_ff_1 (.S(RUN), .C(CLK), .R(counter_1_ovf), .Q(rs_ff_1_q));  // open: nQ
  not not_1 (not_1_out, CLK);
  Counter #(.Bits(4)) counter_1 (.en(rs_ff_1_q), .C(CLK), .clr(counter_1_ovf), .out(ADDR), .ovf(counter_1_ovf));
  nand nand_1 (nPULSE, rs_ff_1_q, not_1_out);

  // Notes on the sheet:
  //   CLK: Hz: 3
endmodule
