// Digital circuit Ctrl.dig as structural Verilog
module Ctrl (
  input  nCLK,
  input  RESET,
  input  IR_4,
  input  IR_5,
  input  IR_6,
  input  IR_7,
  input  CF,
  input  ZF,
  output HLT,
  output nMI,
  output RI,
  output nRO,
  output nIO,
  output nII,
  output nAI,
  output nAO,
  output nEO,
  output SU,
  output nBI,
  output OI,
  output CE,
  output nCO,
  output nJ,
  output nFI,
  output CLR,
  output nCLR,
  output [15:0] DBGC,
  output [7:0] DBGS
);

  wire _74138_1_p1, nand_1_out, nand_3_out;

  nand nand_1 (nand_1_out, nand_3_out, nand_3_out);
  nand nand_2 (nCLR, RESET, RESET);
  // _74161 _74161_1: pin names not known; wires that end beside it: 1'b0, 1'b1, nCLK, 1'b1, 1'b1, 1'b1, 1'b0, nand_1_out, DBGS[0], DBGS[1], DBGS[2]
  nand nand_3 (nand_3_out, nCLR, _74138_1_p1);
  nand nand_4 (CLR, nCLR, nCLR);
  // _74138 _74138_1: pin names not known; wires that end beside it: _74138_1_p1, DBGS[3], DBGS[4], DBGS[5], DBGS[6], DBGS[7], DBGS[2], DBGS[1], DBGS[0], 1'b0, 1'b0, 1'b1, 1'b0, 1'b1
  ROM rom_1 (
    .A_0(DBGS[0]), .A_1(DBGS[1]), .A_2(DBGS[2]), .A_3(IR_4), .A_4(IR_5), .A_5(IR_6), .A_6(IR_7), .A_7(1'b0),
    .A_8(CF), .A_9(ZF), .A_10(1'b0), .nCE(1'b0), .D_0(DBGC[7]), .D_1(DBGC[6]), .D_2(DBGC[5]), .D_3(DBGC[4]),
    .D_4(DBGC[3]), .D_5(DBGC[2]), .D_6(DBGC[1]), .D_7(DBGC[0]));
  ROM rom_2 (
    .A_0(DBGS[0]), .A_1(DBGS[1]), .A_2(DBGS[2]), .A_3(IR_4), .A_4(IR_5), .A_5(IR_6), .A_6(IR_7), .A_7(1'b1),
    .A_8(CF), .A_9(ZF), .A_10(1'b0), .nCE(1'b0), .D_0(DBGC[15]), .D_1(DBGC[14]), .D_2(DBGC[13]), .D_3(CE),
    .D_4(DBGC[11]), .D_5(DBGC[10]), .D_6(DBGC[9]), .D_7(DBGC[8]));
  not not_1 (nAO, DBGC[7]);
  not not_2 (nAI, DBGC[6]);
  not not_3 (nII, DBGC[5]);
  not not_4 (nIO, DBGC[4]);
  not not_5 (nRO, DBGC[3]);
  not not_6 (nMI, DBGC[1]);
  not not_7 (nFI, DBGC[15]);
  not not_8 (nJ, DBGC[14]);
  not not_9 (nCO, DBGC[13]);
  not not_10 (nBI, DBGC[10]);
  not not_11 (nEO, DBGC[8]);

  assign DBGC[12] = CE;
  assign HLT = DBGC[0];
  assign OI = DBGC[11];
  assign RI = DBGC[2];
  assign SU = DBGC[9];

  // Other names for the same wires on the sheet: DBG_0 = DBGS[0]; DBG_1 = DBGS[1]; DBG_2 = DBGS[2]; DBG_3 = DBGS[3];
  //   DBG_4 = DBGS[4]; DBG_5 = DBGS[5]; DBG_6 = DBGS[6]; DBG_7 = DBGS[7]; nRI = DBGC[2]

  // Notes on the sheet:
  //   HLT: Halt
  //   nCLK: > Clock
  //   nMI: MAR in
  //   RI: RAM in
  //   nRO: RAM out
  //   nIO: Input Register Out
  //   nII: Instruction Register In
  //   nAI: A Register In
  //   nAO: A Register Out
  //   SU: Subtract
  //   nBI: B Register In
  //   OI: Output Register In
  //   CE: Program Counter Enable
  //   nCO: Program Counter Out
  //   nFI: Flag Register In
  //   RESET: > Reset
  //   CLR: Clear
  //   nCLR: Clear
  //   DBGC: Debug Control Bus
  //   IR_4: > Instr Reg, bit 4
  //   IR_5: > Instr Reg, bit 5
  //   IR_6: > Instr Reg, bit 6
  //   IR_7: > Instr Reg, bit 7
  //   CF: > Carry Flag
  //   ZF: > Zero Flag
  //   DBGS: Debug Step
endmodule
