// Digital circuit LED7-Driver.dig as structural Verilog
module LED7_Driver (
  input  [3:0] nSEL,
  input  [7:0] A_P_in,
  output [15:0] LA_D,
  output [15:0] LE_P
);

  wire SEL_1, SEL_2, SEL_3, SEL_4;

  // _74374 _74374_1: pin names not known; wires that end beside it: LA_D[15], LA_D[14], LA_D[13], LA_D[12], LE_P[15], LE_P[14], LE_P[13], LE_P[12], 1'b0, 1'b1, SEL_4, A_P_in[6], A_P_in[5], A_P_in[4], A_P_in[3], A_P_in[2], A_P_in[1], A_P_in[0], A_P_in[7], 1'b0
  // _74374 _74374_2: pin names not known; wires that end beside it: LA_D[11], LA_D[10], LA_D[9], LA_D[8], LE_P[11], LE_P[10], LE_P[9], LE_P[8], 1'b0, 1'b1, SEL_3, A_P_in[6], A_P_in[5], A_P_in[4], A_P_in[3], A_P_in[2], A_P_in[1], A_P_in[0], A_P_in[7], 1'b0
  Seven_Seg seven_seg_1 (
    .a(LA_D[15]), .b(LA_D[14]), .c(LA_D[13]), .d(LA_D[12]), .e(LE_P[15]), .f(LE_P[14]), .g(LE_P[13]),
    .dp(LE_P[12]));
  Seven_Seg seven_seg_2 (
    .a(LA_D[11]), .b(LA_D[10]), .c(LA_D[9]), .d(LA_D[8]), .e(LE_P[11]), .f(LE_P[10]), .g(LE_P[9]),
    .dp(LE_P[8]));
  Seven_Seg seven_seg_3 (
    .a(LA_D[7]), .b(LA_D[6]), .c(LA_D[5]), .d(LA_D[4]), .e(LE_P[7]), .f(LE_P[6]), .g(LE_P[5]), .dp(LE_P[4]));
  Seven_Seg seven_seg_4 (
    .a(LA_D[3]), .b(LA_D[2]), .c(LA_D[1]), .d(LA_D[0]), .e(LE_P[3]), .f(LE_P[2]), .g(LE_P[1]), .dp(LE_P[0]));
  // _74374 _74374_3: pin names not known; wires that end beside it: LA_D[7], LA_D[6], LA_D[5], LA_D[4], LE_P[7], LE_P[6], LE_P[5], LE_P[4], 1'b0, 1'b1, SEL_2, A_P_in[6], A_P_in[5], A_P_in[4], A_P_in[3], A_P_in[2], A_P_in[1], A_P_in[0], A_P_in[7], 1'b0
  // _74374 _74374_4: pin names not known; wires that end beside it: LA_D[3], LA_D[2], LA_D[1], LA_D[0], LE_P[3], LE_P[2], LE_P[1], LE_P[0], 1'b0, 1'b1, SEL_1, A_P_in[6], A_P_in[5], A_P_in[4], A_P_in[3], A_P_in[2], A_P_in[1], A_P_in[0], A_P_in[7], 1'b0
  not not_1 (SEL_4, nSEL[3]);
  not not_2 (SEL_3, nSEL[2]);
  not not_3 (SEL_2, nSEL[1]);
  not not_4 (SEL_1, nSEL[0]);

  // Other names for the same wires on the sheet: L2A_D[3:0] = LA_D[7:4]; L2E_P[3:0] = LE_P[7:4];
  //   L1A_D[3:0] = LA_D[3:0]; L1E_P[3:0] = LE_P[3:0]; L3A_D[3:0] = LA_D[11:8]; L3E_P[3:0] = LE_P[11:8];
  //   L4A_D[3:0] = LA_D[15:12]; L4E_P[3:0] = LE_P[15:12]

  // Notes on the sheet:
  //   nSEL: default 1
endmodule
