// Digital circuit MAR.dig as structural Verilog
module MAR (
  input  BUS_3,
  input  BUS_2,
  input  BUS_1,
  input  BUS_0,
  input  nMI,
  input  CLR,
  input  PA_0,
  input  PA_1,
  input  PA_2,
  input  PA_3,
  input  nPROG,
  input  CLK,
  output A_0,
  output A_1,
  output A_2,
  output A_3,
  output [3:0] DBG
);

  wire _74173_1_p13, _74173_1_p14, _74173_1_p15, _74173_1_p16;

  // _74173 _74173_1: pin names not known; wires that end beside it: 1'b1, 1'b0, BUS_3, BUS_2, BUS_1, BUS_0, nMI, nMI, CLK, CLR, 1'b0, 1'b0, _74173_1_p13, _74173_1_p14, _74173_1_p15, _74173_1_p16
  // _74157 _74157_1: pin names not known; wires that end beside it: PA_3, PA_2, PA_1, PA_0, _74173_1_p13, _74173_1_p14, _74173_1_p15, _74173_1_p16, nPROG, 1'b0, 1'b1, 1'b0, A_3, A_2, A_1, A_0

  assign DBG = {A_3, A_2, A_1, A_0};

  // Notes on the sheet:
  //   nMI: Memory In, default 1
  //   CLR: Clear
  //   nPROG: Select; 0 = DATA, 1 = BUS, default 1
endmodule
