// Digital circuit Main.dig as structural Verilog
module Main (
  input  clk,
  input  Program,
  input  clk_2,
  input  clk_3
);

  wire a_register_1_p9, a_register_1_p10, a_register_1_p11, a_register_1_p12, a_register_1_p13,
       a_register_1_p14, a_register_1_p15, a_register_1_p16, a_register_1_p18, a_register_1_p19, ALU_cf,
       ALU_zf, b_register_1_p9, b_register_1_p10, b_register_1_p11, b_register_1_p12, b_register_1_p13,
       b_register_1_p14, b_register_1_p15, b_register_1_p16, b_register_1_p18, CLK_t, clock_1_dbg, CLR,
       Controller_p10, Controller_p11, Controller_p13, Controller_p14, Controller_p15, Controller_p16,
       Controller_p18, Controller_p30, Controller_p31, Controller_p32, i_register_1_p9, i_register_1_p10,
       i_register_1_p11, i_register_1_p12, i_register_1_p14, i_register_1_p15, LOAD_out, MAR_p2, MAR_p7,
       MAR_p10, MAR_p12, MAR_p15, nCLK, nCLR, not_1_out, not_2_out, not_3_out, nPULSE, nPULSE1,
       Out_Register_p15, Step_out, switchdt_1_p1, switchdt_2_p1;
  wire [3:0] a_register_1_p17, a_register_1_p17_2, Addr1, ALU_dbg, ALU_dbg_2, b_register_1_p17,
       b_register_1_p17_2, i_register_1_p13, i_register_1_p13_2, led7_driver_p3, MAR_p1, PADDR, pc_1_bus_3,
       pc_1_dbg, ram_1_bus_7, ram_1_dbg, ram_1_dbg_2;
  wire [7:0] Controller_p26, Data1, led7_driver_p4, PDATA;
  wire [9:8] ALU_dbg_3;
  wire [15:0] Controller_p25, instr_display_disp, led7_driver_p1, led7_driver_p2;

  Button LOAD (.out(LOAD_out));
  DipSwitch _8 (.out(Addr1[3]));
  Addr_Counter Addr_Cntr (.RUN(LOAD_out), .CLK(clk_2), .ADDR(PADDR), .nPULSE(nPULSE));
  DipSwitch _4 (.out(Addr1[2]));
  DipSwitch _2 (.out(Addr1[1]));
  DipSwitch _1 (.out(Addr1[0]));
  DipSwitch _128 (.out(Data1[7]));
  DipSwitch _64 (.out(Data1[6]));
  DipSwitch _32 (.out(Data1[5]));
  LED led_1 (.in(Program));
  DipSwitch _8_2 (.out(Data1[3]));
  DipSwitch _4_2 (.out(Data1[2]));
  DipSwitch _2_2 (.out(Data1[1]));
  DipSwitch _16 (.out(Data1[4]));
  ROM #(.AddrBits(4), .Bits(8)) rom_1 (.A(PADDR), .sel(Program), .D(PDATA));
  not not_1 (not_1_out, Program);
  DipSwitch _1_2 (.out(Data1[0]));
  Button Pulse (.out(nPULSE1));
  Seven_Seg_Hex seven_seg_hex_1 (.d(ram_1_dbg_2), .dp(1'b0));
  Seven_Seg seven_seg_1 (
    .a(led7_driver_p1[15]), .b(led7_driver_p1[14]), .c(led7_driver_p1[13]), .d(led7_driver_p1[12]),
    .e(led7_driver_p2[15]), .f(led7_driver_p2[14]), .g(led7_driver_p2[13]), .dp(led7_driver_p2[12]));
  Seven_Seg_Hex seven_seg_hex_2 (.d(pc_1_dbg), .dp(1'b0));
  Seven_Seg_Hex seven_seg_hex_3 (.d(MAR_p1), .dp(1'b0));
  Seven_Seg_Hex seven_seg_hex_4 (.d(ram_1_dbg), .dp(1'b0));
  Seven_Seg seven_seg_2 (
    .a(led7_driver_p1[11]), .b(led7_driver_p1[10]), .c(led7_driver_p1[9]), .d(led7_driver_p1[8]),
    .e(led7_driver_p2[11]), .f(led7_driver_p2[10]), .g(led7_driver_p2[9]), .dp(led7_driver_p2[8]));
  LED _8_3 (.in(pc_1_dbg[3]));
  LED _8_4 (.in(MAR_p1[3]));
  LED _7 (.in(ram_1_dbg_2[3]));
  Seven_Seg seven_seg_3 (
    .a(led7_driver_p1[7]), .b(led7_driver_p1[6]), .c(led7_driver_p1[5]), .d(led7_driver_p1[4]),
    .e(led7_driver_p2[7]), .f(led7_driver_p2[6]), .g(led7_driver_p2[5]), .dp(led7_driver_p2[4]));
  LED _4_3 (.in(pc_1_dbg[2]));
  LED _2_3 (.in(pc_1_dbg[1]));
  LED _4_4 (.in(MAR_p1[2]));
  LED _2_4 (.in(MAR_p1[1]));
  LED _6 (.in(ram_1_dbg_2[2]));
  LED _5 (.in(ram_1_dbg_2[1]));
  Seven_Seg seven_seg_4 (
    .a(led7_driver_p1[3]), .b(led7_driver_p1[2]), .c(led7_driver_p1[1]), .d(led7_driver_p1[0]),
    .e(led7_driver_p2[3]), .f(led7_driver_p2[2]), .g(led7_driver_p2[1]), .dp(led7_driver_p2[0]));
  LED Unsigned (.in(not_2_out));
  LED Signed (.in(switchdt_1_p1));
  LED _1_3 (.in(pc_1_dbg[0]));
  LED _1_4 (.in(MAR_p1[0]));
  LED _4_5 (.in(ram_1_dbg_2[0]));
  LED _3 (.in(ram_1_dbg[3]));
  not not_2 (not_2_out, switchdt_1_p1);
  // SwitchDT switchdt_1: pin names not known; wires that end beside it: switchdt_1_p1, 1'b1, 1'b0
  LED _2_5 (.in(ram_1_dbg[2]));
  LED _1_5 (.in(ram_1_dbg[1]));
  // LED7_Driver led7_driver: pin names not known; wires that end beside it: led7_driver_p1, led7_driver_p2, led7_driver_p3, led7_driver_p4
  LED _0 (.in(ram_1_dbg[0]));
  LED Run (.in(switchdt_2_p1));
  LED Single_Step (.in(not_3_out));
  not not_3 (not_3_out, switchdt_2_p1);
  // SwitchDT switchdt_2: pin names not known; wires that end beside it: switchdt_2_p1, 1'b1, 1'b0
  PC pc_1 (
    .DBG(pc_1_dbg), .nCO(Controller_p15), .nJ(Controller_p14), .CE(Controller_p13), .nCLR(nCLR), .CLK(CLK_t),
    .BUS_0(pc_1_bus_3[0]), .BUS_1(pc_1_bus_3[1]), .BUS_2(pc_1_bus_3[2]), .BUS_3(pc_1_bus_3[3]));
  // MAR MAR: pin names not known; wires that end beside it: MAR_p1, MAR_p2, not_1_out, CLR, CLK_t, PADDR[3], MAR_p7, MAR_p7, PADDR[2], MAR_p10, PADDR[1], MAR_p12, MAR_p12, PADDR[0], MAR_p15, pc_1_bus_3[0], pc_1_bus_3[1], pc_1_bus_3[2], pc_1_bus_3[3]
  RAM ram_1 (
    .A2(MAR_p10), .A1(MAR_p15), .DBG({ram_1_dbg_2, ram_1_dbg}), .RI(Controller_p11), .nRO(Controller_p10),
    .nPROG(not_1_out), .PDATA(PDATA), .nPULSE(nPULSE), .CLK(CLK_t), .BUS_0(pc_1_bus_3[0]),
    .BUS_1(pc_1_bus_3[1]), .BUS_2(pc_1_bus_3[2]), .BUS_3(pc_1_bus_3[3]), .BUS_4(ram_1_bus_7[0]),
    .BUS_5(ram_1_bus_7[1]), .BUS_6(ram_1_bus_7[2]), .BUS_7(ram_1_bus_7[3]));  // open: A3, A0
  // Out_Register Out_Register: pin names not known; wires that end beside it: clk_3, led7_driver_p3[0], led7_driver_p3[1], led7_driver_p3[2], led7_driver_p3[3], led7_driver_p4[0], led7_driver_p4[1], led7_driver_p4[2], led7_driver_p4[3], led7_driver_p4[4], led7_driver_p4[5], led7_driver_p4[6], led7_driver_p4[7], switchdt_1_p1, Out_Register_p15, nCLR, CLK_t, pc_1_bus_3[0], pc_1_bus_3[1], pc_1_bus_3[2], pc_1_bus_3[3], ram_1_bus_7[0], ram_1_bus_7[1], ram_1_bus_7[2], ram_1_bus_7[3]
  Clock clock_1 (
    .DBG(clock_1_dbg), .HLT(Controller_p18), .CLK(CLK_t), .nCLK(nCLK), .XCLK(clk), .MODE(switchdt_2_p1),
    .STEP(Step_out));
  LED _7_2 (.in(ram_1_bus_7[3]));
  LED u_CLK (.in(clock_1_dbg));
  LED _6_2 (.in(ram_1_bus_7[2]));
  LED _5_2 (.in(ram_1_bus_7[1]));
  LED _4_6 (.in(ram_1_bus_7[0]));
  LED _3_2 (.in(pc_1_bus_3[3]));
  Button Step (.out(Step_out));
  LED _2_6 (.in(pc_1_bus_3[2]));
  LED _1_6 (.in(pc_1_bus_3[1]));
  LED _0_2 (.in(pc_1_bus_3[0]));
  Seven_Seg_Hex seven_seg_hex_5 (.d(ram_1_bus_7), .dp(1'b0));
  // A_Register a_register_1: pin names not known; wires that end beside it: pc_1_bus_3[0], pc_1_bus_3[1], pc_1_bus_3[2], pc_1_bus_3[3], ram_1_bus_7[0], ram_1_bus_7[1], ram_1_bus_7[2], ram_1_bus_7[3], a_register_1_p9, a_register_1_p10, a_register_1_p11, a_register_1_p12, a_register_1_p13, a_register_1_p14, a_register_1_p15, a_register_1_p16, {a_register_1_p17_2, a_register_1_p17}, a_register_1_p18, a_register_1_p19, CLR, CLK_t
  ALU ALU (
    .DBG({ALU_dbg_3, ALU_dbg_2, ALU_dbg}), .CF(ALU_cf), .ZF(ALU_zf), .nEO(Controller_p32),
    .SU(Controller_p31), .nFI(Controller_p30), .CLR(CLR), .CLK(CLK_t), .B_7(b_register_1_p9),
    .B_6(b_register_1_p10), .B_5(b_register_1_p11), .B_4(b_register_1_p12), .B_3(b_register_1_p13),
    .B_2(b_register_1_p14), .B_1(b_register_1_p15), .B_0(b_register_1_p16), .A_7(a_register_1_p9),
    .A_6(a_register_1_p10), .A_5(a_register_1_p11), .A_4(a_register_1_p12), .A_3(a_register_1_p13),
    .A_2(a_register_1_p14), .A_1(a_register_1_p15), .A_0(a_register_1_p16), .BUS_0(pc_1_bus_3[0]),
    .BUS_1(pc_1_bus_3[1]), .BUS_2(pc_1_bus_3[2]), .BUS_3(pc_1_bus_3[3]), .BUS_4(ram_1_bus_7[0]),
    .BUS_5(ram_1_bus_7[1]), .BUS_6(ram_1_bus_7[2]), .BUS_7(ram_1_bus_7[3]));
  // B_Register b_register_1: pin names not known; wires that end beside it: pc_1_bus_3[0], pc_1_bus_3[1], pc_1_bus_3[2], pc_1_bus_3[3], ram_1_bus_7[0], ram_1_bus_7[1], ram_1_bus_7[2], ram_1_bus_7[3], b_register_1_p9, b_register_1_p10, b_register_1_p11, b_register_1_p12, b_register_1_p13, b_register_1_p14, b_register_1_p15, b_register_1_p16, {b_register_1_p17_2, b_register_1_p17}, b_register_1_p18, 1'b0, CLR, CLK_t
  // I_Register i_register_1: pin names not known; wires that end beside it: pc_1_bus_3[0], pc_1_bus_3[1], pc_1_bus_3[2], pc_1_bus_3[3], ram_1_bus_7[0], ram_1_bus_7[1], ram_1_bus_7[2], ram_1_bus_7[3], i_register_1_p9, i_register_1_p10, i_register_1_p11, i_register_1_p12, {i_register_1_p13_2, i_register_1_p13}, i_register_1_p14, i_register_1_p15, CLR, CLK_t
  // Ctrl Controller: pin names not known; wires that end beside it: ram_1_bus_7[3], ram_1_bus_7[2], ram_1_bus_7[1], ram_1_bus_7[0], pc_1_bus_3[3], pc_1_bus_3[2], pc_1_bus_3[1], pc_1_bus_3[0], Out_Register_p15, Controller_p10, Controller_p11, MAR_p2, Controller_p13, Controller_p14, Controller_p15, Controller_p16, i_register_1_p9, Controller_p18, i_register_1_p10, CLR, i_register_1_p11, nCLR, i_register_1_p12, CLK_t, Controller_p25, Controller_p26, i_register_1_p15, i_register_1_p14, b_register_1_p18, Controller_p30, Controller_p31, Controller_p32, ALU_zf, ALU_cf, a_register_1_p19, a_register_1_p18
  Seven_Seg_Hex seven_seg_hex_6 (.d(pc_1_bus_3), .dp(1'b0));
  Button Reset (.out(Controller_p16));
  LED _7_3 (.in(a_register_1_p17_2[3]));
  LED _7_4 (.in(ALU_dbg_2[3]));
  LED _7_5 (.in(b_register_1_p17_2[3]));
  LED Inst_3 (.in(i_register_1_p13_2[3]));
  LED T1 (.in(Controller_p26[7]));
  LED HLT (.in(Controller_p25[0]));
  LED _6_3 (.in(a_register_1_p17_2[2]));
  LED _5_3 (.in(a_register_1_p17_2[1]));
  LED _6_4 (.in(ALU_dbg_2[2]));
  LED _5_4 (.in(ALU_dbg_2[1]));
  LED _6_5 (.in(b_register_1_p17_2[2]));
  LED _5_5 (.in(b_register_1_p17_2[1]));
  LED Inst_2 (.in(i_register_1_p13_2[2]));
  LED Inst_1 (.in(i_register_1_p13_2[1]));
  LED T3 (.in(Controller_p26[5]));
  LED T2 (.in(Controller_p26[6]));
  LED MI (.in(Controller_p25[1]));
  LED RI (.in(Controller_p25[2]));
  LED _4_7 (.in(a_register_1_p17_2[0]));
  LED _3_3 (.in(a_register_1_p17[3]));
  LED _4_8 (.in(ALU_dbg_2[0]));
  LED _3_4 (.in(ALU_dbg[3]));
  LED _4_9 (.in(b_register_1_p17_2[0]));
  LED _3_5 (.in(b_register_1_p17[3]));
  LED Data_3 (.in(i_register_1_p13[3]));
  LED Inst_0 (.in(i_register_1_p13_2[0]));
  LED T5 (.in(Controller_p26[3]));
  LED T4 (.in(Controller_p26[4]));
  LED RO (.in(Controller_p25[3]));
  LED IO (.in(Controller_p25[4]));
  LED _2_7 (.in(a_register_1_p17[2]));
  LED _1_7 (.in(a_register_1_p17[1]));
  LED _2_8 (.in(ALU_dbg[2]));
  LED _1_8 (.in(ALU_dbg[1]));
  LED _2_9 (.in(b_register_1_p17[2]));
  LED _1_9 (.in(b_register_1_p17[1]));
  LED Data_2 (.in(i_register_1_p13[2]));
  LED Data_1 (.in(i_register_1_p13[1]));
  LED II (.in(Controller_p25[5]));
  LED AI (.in(Controller_p25[6]));
  Seven_Seg_Hex seven_seg_hex_7 (.d(a_register_1_p17_2), .dp(1'b0));
  LED _0_3 (.in(a_register_1_p17[0]));
  Seven_Seg_Hex seven_seg_hex_8 (.d(ALU_dbg_2), .dp(1'b0));
  LED _0_4 (.in(ALU_dbg[0]));
  Seven_Seg_Hex seven_seg_hex_9 (.d(b_register_1_p17_2), .dp(1'b0));
  LED _0_5 (.in(b_register_1_p17[0]));
  Seven_Seg_Hex seven_seg_hex_10 (.d(i_register_1_p13_2), .dp(1'b0));
  LED Data_0 (.in(i_register_1_p13[0]));
  LED EO (.in(Controller_p25[8]));
  LED AO (.in(Controller_p25[7]));
  Seven_Seg_Hex seven_seg_hex_11 (.d(a_register_1_p17), .dp(1'b0));
  Seven_Seg_Hex seven_seg_hex_12 (.d(ALU_dbg), .dp(1'b0));
  Seven_Seg_Hex seven_seg_hex_13 (.d(b_register_1_p17), .dp(1'b0));
  Seven_Seg_Hex seven_seg_hex_14 (.d(i_register_1_p13), .dp(1'b0));
  LED BI (.in(Controller_p25[10]));
  LED SU (.in(Controller_p25[9]));
  Instr_Display instr_display (.INST({i_register_1_p13_2, i_register_1_p13}), .DISP(instr_display_disp));
  LED CE (.in(Controller_p25[12]));
  LED OI (.in(Controller_p25[11]));
  LED CF (.in(ALU_dbg_3[8]));
  LED ZF (.in(ALU_dbg_3[9]));
  LED J (.in(Controller_p25[14]));
  LED CO (.in(Controller_p25[13]));
  LED FI (.in(Controller_p25[15]));
  LED NOP (.in(instr_display_disp[0]));
  LED LDA (.in(instr_display_disp[1]));
  LED ADD (.in(instr_display_disp[2]));
  LED SUB (.in(instr_display_disp[3]));
  LED STA (.in(instr_display_disp[4]));
  LED LDI (.in(instr_display_disp[5]));
  LED JMP (.in(instr_display_disp[6]));
  LED JC (.in(instr_display_disp[7]));
  LED JZ (.in(instr_display_disp[8]));
  LED led_2 (.in(instr_display_disp[9]));
  LED led_3 (.in(instr_display_disp[10]));
  LED led_4 (.in(instr_display_disp[11]));
  LED led_5 (.in(instr_display_disp[12]));
  LED led_6 (.in(instr_display_disp[13]));
  LED OUT (.in(instr_display_disp[14]));
  LED HLT_2 (.in(instr_display_disp[15]));

  // Notes on the sheet:
  //   clk_2: Hz: 10
  //   clk_3: Hz: 4
  //   Addr
  //   Value
  //   contents of rom_1 (hex, n*v repeats v):
  //   1e,2f,e0,f0,0,0,0,0,0,0,0,0,0,0,4,5
  //   PC
  //   MAR
  //   RAM
  //   Bus
  //   A Register
  //   Adder
  //   B Register
  //   Instr Register
  //   Step
  //   Control Bus
endmodule
