// Digital circuit Out-Register.dig as structural Verilog
module Out_Register (
  input  BUS_0,
  input  BUS_1,
  input  BUS_2,
  input  BUS_3,
  input  BUS_4,
  input  BUS_5,
  input  BUS_6,
  input  BUS_7,
  input  XCLK,
  input  MODE,
  input  nCLR,
  input  OI,
  input  CLK,
  output A,
  output B,
  output C,
  output D,
  output E,
  output F,
  output G,
  output DP,
  output nS1,
  output nS2,
  output nS3,
  output nS4
);

  wire _7476_1_p8, _7476_1_p14, _74173_1_p13, _74173_1_p14, _74173_1_p15, _74173_1_p16, _74173_2_p13,
       _74173_2_p14, _74173_2_p15, _74173_2_p16, CLR, nOI;

  not not_1 (nOI, OI);
  not not_2 (CLR, nCLR);
  // _74173 _74173_1: pin names not known; wires that end beside it: 1'b1, 1'b0, BUS_0, BUS_1, BUS_2, BUS_3, nOI, nOI, CLK, CLR, 1'b0, 1'b0, _74173_1_p13, _74173_1_p14, _74173_1_p15, _74173_1_p16
  // _74173 _74173_2: pin names not known; wires that end beside it: 1'b1, 1'b0, BUS_4, BUS_5, BUS_6, BUS_7, nOI, nOI, CLK, CLR, 1'b0, 1'b0, _74173_2_p13, _74173_2_p14, _74173_2_p15, _74173_2_p16
  // _7476 _7476_1: pin names not known; wires that end beside it: 1'b1, 1'b1, XCLK, 1'b1, 1'b1, 1'b1, 1'b1, _7476_1_p8, 1'b1, 1'b1, 1'b1, 1'b0, _7476_1_p8, _7476_1_p14
  ROM_Out rom_out_1 (
    .A_0(_74173_1_p13), .A_1(_74173_1_p14), .A_2(_74173_1_p15), .A_3(_74173_1_p16), .A_4(_74173_2_p13),
    .A_5(_74173_2_p14), .A_6(_74173_2_p15), .A_7(_74173_2_p16), .A_8(_7476_1_p8), .A_9(_7476_1_p14),
    .A_10(MODE), .nCE(1'b0), .D_0(A), .D_1(B), .D_2(C), .D_3(D), .D_4(E), .D_5(F), .D_6(G), .D_7(DP));
  // _74139 _74139_1: pin names not known; wires that end beside it: 1'b0, _7476_1_p8, _7476_1_p14, 1'b0, 1'b0, 1'b0, 1'b1, 1'b0, nS1, nS2, nS3, nS4
  Seven_Seg seven_seg_1 (.a(G), .b(F), .c(E), .d(D), .e(C), .f(B), .g(A), .dp(DP));

  // Other names for the same wires on the sheet: S1 = nS1; S2 = nS2; S3 = nS3; S4 = nS4

  // Notes on the sheet:
  //   nCLR: default 1
endmodule
