// Digital circuit ROM.dig as structural Verilog
module ROM (
  input  A_0,
  input  A_1,
  input  A_2,
  input  A_3,
  input  A_4,
  input  A_5,
  input  A_6,
  input  A_7,
  input  A_8,
  input  A_9,
  input  A_10,
  input  nCE,
  output D_0,
  output D_1,
  output D_2,
  output D_3,
  output D_4,
  output D_5,
  output D_6,
  output D_7
);

  wire not_1_out;

  not not_1 (not_1_out, nCE);
  ROM #(.AddrBits(11), .Bits(8)) rom_1 (
    .A({A_10, A_9, A_8, A_7, A_6, A_5, A_4, A_3, A_2, A_1, A_0}), .sel(not_1_out),
    .D({D_7, D_6, D_5, D_4, D_3, D_2, D_1, D_0}));

  // Notes on the sheet:
  //   contents of rom_1 (hex, n*v repeats v):
  //   40,14,0,0,0,0,0,0,40,14,48,12,0,0,0,0,40,14,48,10,2,0,0,0,40,14,48,10,2,0,0,0,40,
  //   14,48,21,0,0,0,0,40,14,a,0,0,0,0,0,40,14,8,0,0,0,0,0,40,14,0,0,0,0,0,0,40,14,0,0,
  //   0,0,0,0,40,14,0,0,0,0,0,0,40,14,0,0,0,0,0,0,40,14,0,0,0,0,0,0,40,14,0,0,0,0,0,0,40,
  //   14,0,0,0,0,0,0,40,14,1,0,0,0,0,0,40,14,80,0,0,0,0,0,4,8,0,0,0,0,0,0,4,8,0,0,0,0,0,
  //   0,4,8,0,20,81,0,0,0,4,8,0,20,c1,0,0,0,4,8,0,0,0,0,0,0,4,8,0,0,0,0,0,0,4,8,2,0,0,0,
  //   0,0,4,8,0,0,0,0,0,0,4,8,0,0,0,0,0,0,4,8,0,0,0,0,0,0,4,8,0,0,0,0,0,0,4,8,0,0,0,0,0,
  //   0,4,8,0,0,0,0,0,0,4,8,0,0,0,0,0,0,4,8,10,0,0,0,0,0,4,8,0,0,0,0,0,0,40,14,0,0,0,0,
  //   0,0,40,14,48,12,0,0,0,0,40,14,48,10,2,0,0,0,40,14,48,10,2,0,0,0,40,14,48,21,0,0,0,
  //   0,40,14,a,0,0,0,0,0,40,14,8,0,0,0,0,0,40,14,8,0,0,0,0,0,40,14,0,0,0,0,0,0,40,14,0,
  //   0,0,0,0,0,40,14,0,0,0,0,0,0,40,14,0,0,0,0,0,0,40,14,0,0,0,0,0,0,40,14,0,0,0,0,0,0,
  //   40,14,1,0,0,0,0,0,40,14,80,0,0,0,0,0,4,8,0,0,0,0,0,0,4,8,0,0,0,0,0,0,4,8,0,20,81,
  //   0,0,0,4,8,0,20,c1,0,0,0,4,8,0,0,0,0,0,0,4,8,0,0,0,0,0,0,4,8,2,0,0,0,0,0,4,8,2,0,0,
  //   0,0,0,4,8,0,0,0,0,0,0,4,8,0,0,0,0,0,0,4,8,0,0,0,0,0,0,4,8,0,0,0,0,0,0,4,8,0,0,0,0,
  //   0,0,4,8,0,0,0,0,0,0,4,8,10,0,0,0,0,0,4,8,0,0,0,0,0,0,40,14,0,0,0,0,0,0,40,14,48,12,
  //   0,0,0,0,40,14,48,10,2,0,0,0,40,14,48,10,2,0,0,0,40,14,48,21,0,0,0,0,40,14,a,0,0,0,
  //   0,0,40,14,8,0,0,0,0,0,40,14,0,0,0,0,0,0,40,14,8,0,0,0,0,0,40,14,0,0,0,0,0,0,40,14,
  //   0,0,0,0,0,0,40,14,0,0,0,0,0,0,40,14,0,0,0,0,0,0,40,14,0,0,0,0,0,0,40,14,1,0,0,0,0,
  //   0,40,14,80,0,0,0,0,0,4,8,0,0,0,0,0,0,4,8,0,0,0,0,0,0,4,8,0,20,81,0,0,0,4,8,0,20,c1,
  //   0,0,0,4,8,0,0,0,0,0,0,4,8,0,0,0,0,0,0,4,8,2,0,0,0,0,0,4,8,0,0,0,0,0,0,4,8,2,0,0,0,
  //   0,0,4,8,0,0,0,0,0,0,4,8,0,0,0,0,0,0,4,8,0,0,0,0,0,0,4,8,0,0,0,0,0,0,4,8,0,0,0,0,0,
  //   0,4,8,10,0,0,0,0,0,4,8,0,0,0,0,0,0,40,14,0,0,0,0,0,0,40,14,48,12,0,0,0,0,40,14,48,
  //   10,2,0,0,0,40,14,48,10,2,0,0,0,40,14,48,21,0,0,0,0,40,14,a,0,0,0,0,0,40,14,8,0,0,
  //   0,0,0,40,14,8,0,0,0,0,0,40,14,8,0,0,0,0,0,40,14,0,0,0,0,0,0,40,14,0,0,0,0,0,0,40,
  //   14,0,0,0,0,0,0,40,14,0,0,0,0,0,0,40,14,0,0,0,0,0,0,40,14,1,0,0,0,0,0,40,14,80,0,0,
  //   0,0,0,4,8,0,0,0,0,0,0,4,8,0,0,0,0,0,0,4,8,0,20,81,0,0,0,4,8,0,20,c1,0,0,0,4,8,0,0,
  //   0,0,0,0,4,8,0,0,0,0,0,0,4,8,2,0,0,0,0,0,4,8,2,0,0,0,0,0,4,8,2,0,0,0,0,0,4,8,0,0,0,
  //   0,0,0,4,8,0,0,0,0,0,0,4,8,0,0,0,0,0,0,4,8,0,0,0,0,0,0,4,8,0,0,0,0,0,0,4,8,10,0,0,
  //   0,0,0,4,8
endmodule
