// Digital circuit A-Register.dig as structural Verilog
module A_Register (
  input  BUS_0,
  input  BUS_1,
  input  BUS_2,
  input  BUS_3,
  input  BUS_4,
  input  BUS_5,
  input  BUS_6,
  input  BUS_7,
  input  nAI,
  input  nAO,
  input  CLR,
  input  CLK,
  output [7:0] DBG,
  output A_7,
  output A_6,
  output A_5,
  output A_4,
  output A_3,
  output A_2,
  output A_1,
  output A_0
);

  // _74173 _74173_1: pin names not known; wires that end beside it: 1'b1, 1'b0, BUS_0, BUS_1, BUS_2, BUS_3, nAI, nAI, CLK, CLR, 1'b0, 1'b0, A_0, A_1, A_2, A_3
  // _74173 _74173_2: pin names not known; wires that end beside it: 1'b1, 1'b0, BUS_4, BUS_5, BUS_6, BUS_7, nAI, nAI, CLK, CLR, 1'b0, 1'b0, A_4, A_5, A_6, A_7
  // _74245 _74245_1: pin names not known; wires that end beside it: 1'b1, 1'b1, 1'b0, A_0, A_1, A_2, A_3, A_4, A_5, A_6, A_7, nAO, BUS_0, BUS_1, BUS_2, BUS_3, BUS_4, BUS_5, BUS_6, BUS_7

  assign DBG = {A_7, A_6, A_5, A_4, A_3, A_2, A_1, A_0};

  // Notes on the sheet:
  //   nAI: default 1
  //   nAO: default 1
endmodule
