// Digital circuit ALU.dig as structural Verilog
module ALU (
  input  SU,
  input  nEO,
  input  nFI,
  input  CLR,
  input  B_7,
  input  B_6,
  input  B_5,
  input  B_4,
  input  B_3,
  input  B_2,
  input  B_1,
  input  B_0,
  input  A_7,
  input  A_6,
  input  A_5,
  input  A_4,
  input  A_3,
  input  A_2,
  input  A_1,
  input  A_0,
  input  CLK,
  output [9:0] DBG,
  output CF,
  output ZF,
  output BUS_0,
  output BUS_1,
  output BUS_2,
  output BUS_3,
  output BUS_4,
  output BUS_5,
  output BUS_6,
  output BUS_7
);

  wire _74173_1_p4, _74173_1_p5, _74283_1_p6, _74283_1_p10, _74283_1_p11, _74283_1_p12, _74283_1_p13,
       _74283_2_p5, _74283_2_p6, _74283_2_p7, _74283_2_p8, and_2_out, and_3_out, nor_1_out, nor_2_out,
       nor_3_out, nor_4_out;

  // _74173 _74173_1: pin names not known; wires that end beside it: 1'b1, CF, 1'b0, _74173_1_p4, _74173_1_p5, DBG[9], 1'b0, 1'b0, nFI, nFI, CLK, CLR, 1'b0, 1'b0
  // PolarityAwareLED CF: pin names not known; wires that end beside it: CF, 1'b0
  // PolarityAwareLED ZF: pin names not known; wires that end beside it: DBG[9], 1'b0
  and and_1 (_74173_1_p5, and_3_out, and_2_out);
  and and_2 (and_2_out, nor_2_out, nor_1_out);
  and and_3 (and_3_out, nor_4_out, nor_3_out);
  nor nor_1 (nor_1_out, DBG[6], DBG[7]);
  nor nor_2 (nor_2_out, DBG[4], DBG[5]);
  nor nor_3 (nor_3_out, DBG[2], DBG[3]);
  nor nor_4 (nor_4_out, DBG[0], DBG[1]);
  // _74245 _74245_1: pin names not known; wires that end beside it: 1'b1, nEO, 1'b1, BUS_7, 1'b0, BUS_6, DBG[7], BUS_5, DBG[6], BUS_4, DBG[5], BUS_3, DBG[4], BUS_2, DBG[3], BUS_1, DBG[2], BUS_0, DBG[1], DBG[0]
  // _74283 _74283_1: pin names not known; wires that end beside it: _74173_1_p4, DBG[7], DBG[6], DBG[5], DBG[4], _74283_1_p6, 1'b0, 1'b1, _74283_1_p6, _74283_1_p10, _74283_1_p11, _74283_1_p12, _74283_1_p13, A_7, A_6, A_5, A_4, 1'b0, 1'b1, SU
  // _74283 _74283_2: pin names not known; wires that end beside it: DBG[3], DBG[2], DBG[1], DBG[0], _74283_2_p5, _74283_2_p6, _74283_2_p7, _74283_2_p8, A_3, A_2, A_1, A_0
  xor xor_1 (_74283_1_p10, B_7, SU);
  xor xor_2 (_74283_1_p11, B_6, SU);
  xor xor_3 (_74283_1_p12, B_5, SU);
  xor xor_4 (_74283_1_p13, B_4, SU);
  xor xor_5 (_74283_2_p5, B_3, SU);
  xor xor_6 (_74283_2_p6, B_2, SU);
  xor xor_7 (_74283_2_p7, B_1, SU);
  xor xor_8 (_74283_2_p8, B_0, SU);

  assign DBG[8] = CF;
  assign ZF = DBG[9];

  // Notes on the sheet:
  //   nEO: default 1
  //   nFI: default 1
endmodule
