// Digital circuit B-Register.dig as structural Verilog
module B_Register (
  input  BUS_0,
  input  BUS_1,
  input  BUS_2,
  input  BUS_3,
  input  BUS_4,
  input  BUS_5,
  input  BUS_6,
  input  BUS_7,
  input  nBI,
  input  nBO,
  input  CLK,
  input  CLR,
  output [7:0] DBG,
  output B_7,
  output B_6,
  output B_5,
  output B_4,
  output B_3,
  output B_2,
  output B_1,
  output B_0
);

  wire Bus_0_t, Bus_1_t, Bus_2_t, Bus_3_t, Bus_4_t, Bus_5_t, Bus_6_t, Bus_7_t;

  // _74173 _74173_1: pin names not known; wires that end beside it: 1'b1, 1'b0, BUS_0, BUS_1, BUS_2, BUS_3, nBI, nBI, CLK, CLR, 1'b0, 1'b0, B_0, B_1, B_2, B_3
  // _74173 _74173_2: pin names not known; wires that end beside it: 1'b1, 1'b0, BUS_4, BUS_5, BUS_6, BUS_7, nBI, nBI, CLK, CLR, 1'b0, 1'b0, B_4, B_5, B_6, B_7
  // _74245 _74245_1: pin names not known; wires that end beside it: 1'b1, 1'b1, 1'b0, B_0, B_1, B_2, B_3, B_4, B_5, B_6, B_7, nBO, Bus_0_t, Bus_1_t, Bus_2_t, Bus_3_t, Bus_4_t, Bus_5_t, Bus_6_t, Bus_7_t

  assign DBG = {B_7, B_6, B_5, B_4, B_3, B_2, B_1, B_0};

  // Notes on the sheet:
  //   nBI: default 1
  //   nBO: default 1
endmodule
