// Digital circuit Clock.dig as structural Verilog
module Clock (
  input  HLT,
  input  XCLK,
  input  nRUN,
  input  STEP,
  output CLK,
  output nCLK,
  output DBG
);

  wire and_1_out, not_1_out, xor_1_out;

  and and_1 (and_1_out, ~nRUN, XCLK);  // And
  xor xor_1 (xor_1_out, and_1_out, STEP);
  not not_1 (not_1_out, HLT);
  and and_2 (CLK, xor_1_out, not_1_out);
  not not_2 (nCLK, CLK);

  assign DBG = CLK;

  // Notes on the sheet:
  //   nRUN: low = run, high = single step, default 1
endmodule
