// Digital circuit I-Register.dig as structural Verilog
module I_Register (
  input  BUS_0,
  input  BUS_1,
  input  BUS_2,
  input  BUS_3,
  input  BUS_4,
  input  BUS_5,
  input  BUS_6,
  input  BUS_7,
  input  nIO,
  input  nII,
  input  CLR,
  input  CLK,
  output IR_4,
  output IR_5,
  output IR_6,
  output IR_7,
  output [7:0] DBG
);

  // _74173 _74173_1: pin names not known; wires that end beside it: 1'b1, 1'b0, BUS_7, BUS_6, BUS_5, BUS_4, nII, nII, CLK, CLR, 1'b0, 1'b0, DBG[7], DBG[6], DBG[5], DBG[4]
  // _74173 _74173_2: pin names not known; wires that end beside it: 1'b1, 1'b0, BUS_3, BUS_2, BUS_1, BUS_0, nII, nII, CLK, CLR, 1'b0, 1'b0, DBG[3], DBG[2], DBG[1], DBG[0]
  // _74245 _74245_1: pin names not known; wires that end beside it: 1'b1, 1'b1, 1'b0, 1'b0, 1'b0, 1'b0, 1'b0, DBG[3], DBG[2], DBG[1], DBG[0], nIO, BUS_7, BUS_6, BUS_5, BUS_4, BUS_3, BUS_2, BUS_1, BUS_0

  assign IR_4 = DBG[4];
  assign IR_5 = DBG[5];
  assign IR_6 = DBG[6];
  assign IR_7 = DBG[7];

  // Notes on the sheet:
  //   nIO: default 1
endmodule
