// Digital circuit Instr-Display.dig as structural Verilog
module Instr_Display (
  input  [7:0] INST,
  output [15:0] DISP
);

  wire _74154_1_p9, _74154_1_p10, _74154_1_p11, _74154_1_p12, _74154_1_p13, _74154_1_p14, _74154_1_p15,
       _74154_1_p16, _74154_1_p17, _74154_1_p18, _74154_1_p19, _74154_1_p20, _74154_1_p21, _74154_1_p22,
       _74154_1_p23, _74154_1_p24;

  // _74154 _74154_1: pin names not known; wires that end beside it: 1'b1, 1'b0, 1'b0, 1'b0, INST[4], INST[5], INST[6], INST[7], _74154_1_p9, _74154_1_p10, _74154_1_p11, _74154_1_p12, _74154_1_p13, _74154_1_p14, _74154_1_p15, _74154_1_p16, _74154_1_p17, _74154_1_p18, _74154_1_p19, _74154_1_p20, _74154_1_p21, _74154_1_p22, _74154_1_p23, _74154_1_p24
  not not_1 (DISP[0], _74154_1_p9);
  not not_2 (DISP[1], _74154_1_p10);
  not not_3 (DISP[2], _74154_1_p11);
  not not_4 (DISP[3], _74154_1_p12);
  not not_5 (DISP[4], _74154_1_p13);
  not not_6 (DISP[5], _74154_1_p14);
  not not_7 (DISP[6], _74154_1_p15);
  not not_8 (DISP[7], _74154_1_p16);
  not not_9 (DISP[8], _74154_1_p17);
  not not_10 (DISP[9], _74154_1_p18);
  not not_11 (DISP[10], _74154_1_p19);
  not not_12 (DISP[11], _74154_1_p20);
  not not_13 (DISP[12], _74154_1_p21);
  not not_14 (DISP[13], _74154_1_p22);
  not not_15 (DISP[14], _74154_1_p23);
  not not_16 (DISP[15], _74154_1_p24);

  // Notes on the sheet:
  //   INST: 4 Bit instruction code
endmodule
