// Digital circuit Main.dig as structural Verilog
module Main (
  input  clk,
  input  Program,
  input  clk_2,
  input  clk_3,
  input  Signed,
  input  Step_Run
);

  wire a_register_1_a_0, a_register_1_a_1, a_register_1_a_2, a_register_1_a_3, a_register_1_a_4,
       a_register_1_a_5, a_register_1_a_6, a_register_1_a_7, ALU_cf, ALU_zf, b_register_1_b_0,
       b_register_1_b_1, b_register_1_b_2, b_register_1_b_3, b_register_1_b_4, b_register_1_b_5,
       b_register_1_b_6, b_register_1_b_7, CLK_t, clock_1_dbg, CLR, Controller_ce, Controller_hlt,
       Controller_nai, Controller_nao, Controller_nbi, Controller_nco, Controller_neo, Controller_nfi,
       Controller_nii, Controller_nio, Controller_nj, Controller_nmi, Controller_nro, Controller_oi,
       Controller_ri, Controller_su, i_register_1_ir_4, i_register_1_ir_5, i_register_1_ir_6,
       i_register_1_ir_7, LOAD_out, MAR_a_0, MAR_a_1, MAR_a_2, MAR_a_3, nCLK, nCLR, not_1_out, not_2_out,
       programmer_1_nprog, programmer_1_npulse, Pulse_out, Reset_out, Step_out;
  wire [3:0] _1_out, a_register_1_dbg, a_register_1_dbg_2, ALU_dbg, ALU_dbg_2, b_register_1_dbg,
       b_register_1_dbg_2, i_register_1_dbg, i_register_1_dbg_2, MAR_dbg, Out_Register_nsel, PADDR,
       pc_1_bus_0, pc_1_dbg, ram_1_bus_7, ram_1_dbg;
  wire [7:0] _1_2_out, Controller_dbgs, Out_Register_a_p, programmer_1_pdata;
  wire [7:4] ram_1_dbg_2;
  wire [9:8] ALU_dbg_3;
  wire [15:0] Controller_dbgc, instr_display_disp, led7_driver_la_d, led7_driver_le_p;

  Button #(.activeLow("true")) LOAD (.out(LOAD_out));
  not not_1 (not_1_out, Program);
  Programmer programmer_1 (
    .nLOAD(LOAD_out), .BCLK(clk_2), .nSPROG(not_1_out), .PADDR(PADDR), .nPROG(programmer_1_nprog),
    .PDATA(programmer_1_pdata), .nPULSE(programmer_1_npulse), .SADDR(_1_out), .SDATA(_1_2_out),
    .nSPULSE(Pulse_out));
  DipSwitch _8 (.out(_1_out[3]));
  DipSwitch _4 (.out(_1_out[2]));
  DipSwitch _2 (.out(_1_out[1]));
  DipSwitch _1 (.out(_1_out[0]));
  DipSwitch _128 (.out(_1_2_out[7]));
  DipSwitch _64 (.out(_1_2_out[6]));
  DipSwitch _8_2 (.out(_1_2_out[3]));
  DipSwitch _4_2 (.out(_1_2_out[2]));
  DipSwitch _32 (.out(_1_2_out[5]));
  DipSwitch _16 (.out(_1_2_out[4]));
  DipSwitch _2_2 (.out(_1_2_out[1]));
  DipSwitch _1_2 (.out(_1_2_out[0]));
  Seven_Seg_Hex seven_seg_hex_1 (.d(ram_1_dbg_2), .dp(1'b0));
  Button Pulse (.out(Pulse_out));
  Seven_Seg_Hex seven_seg_hex_2 (.d(pc_1_dbg), .dp(1'b0));
  Seven_Seg_Hex seven_seg_hex_3 (.d(MAR_dbg), .dp(1'b0));
  Seven_Seg_Hex seven_seg_hex_4 (.d(ram_1_dbg), .dp(1'b0));
  Seven_Seg seven_seg_1 (
    .a(led7_driver_la_d[15]), .b(led7_driver_la_d[14]), .c(led7_driver_la_d[13]), .d(led7_driver_la_d[12]),
    .e(led7_driver_le_p[15]), .f(led7_driver_le_p[14]), .g(led7_driver_le_p[13]), .dp(led7_driver_le_p[12]));
  LED _8_3 (.in(pc_1_dbg[3]));
  LED _8_4 (.in(MAR_dbg[3]));
  LED _7 (.in(ram_1_dbg_2[7]));
  Seven_Seg seven_seg_2 (
    .a(led7_driver_la_d[11]), .b(led7_driver_la_d[10]), .c(led7_driver_la_d[9]), .d(led7_driver_la_d[8]),
    .e(led7_driver_le_p[11]), .f(led7_driver_le_p[10]), .g(led7_driver_le_p[9]), .dp(led7_driver_le_p[8]));
  not not_2 (not_2_out, Step_Run);
  Button Step (.out(Step_out));
  Button Reset (.out(Reset_out));
  LED _4_3 (.in(pc_1_dbg[2]));
  LED _2_3 (.in(pc_1_dbg[1]));
  LED _4_4 (.in(MAR_dbg[2]));
  LED _2_4 (.in(MAR_dbg[1]));
  LED _6 (.in(ram_1_dbg_2[6]));
  LED _5 (.in(ram_1_dbg_2[5]));
  Seven_Seg seven_seg_3 (
    .a(led7_driver_la_d[7]), .b(led7_driver_la_d[6]), .c(led7_driver_la_d[5]), .d(led7_driver_la_d[4]),
    .e(led7_driver_le_p[7]), .f(led7_driver_le_p[6]), .g(led7_driver_le_p[5]), .dp(led7_driver_le_p[4]));
  LED _1_3 (.in(pc_1_dbg[0]));
  LED _1_4 (.in(MAR_dbg[0]));
  LED _4_5 (.in(ram_1_dbg_2[4]));
  LED _3 (.in(ram_1_dbg[3]));
  Seven_Seg seven_seg_4 (
    .a(led7_driver_la_d[3]), .b(led7_driver_la_d[2]), .c(led7_driver_la_d[1]), .d(led7_driver_la_d[0]),
    .e(led7_driver_le_p[3]), .f(led7_driver_le_p[2]), .g(led7_driver_le_p[1]), .dp(led7_driver_le_p[0]));
  LED _2_5 (.in(ram_1_dbg[2]));
  LED _1_5 (.in(ram_1_dbg[1]));
  LED7_Driver led7_driver (
    .LA_D(led7_driver_la_d), .nSEL(Out_Register_nsel), .A_P_in(Out_Register_a_p), .LE_P(led7_driver_le_p));
  LED _0 (.in(ram_1_dbg[0]));
  PC pc_1 (
    .DBG(pc_1_dbg), .nCO(Controller_nco), .nJ(Controller_nj), .CE(Controller_ce), .nCLR(nCLR), .CLK(CLK_t),
    .BUS_0(pc_1_bus_0[0]), .BUS_1(pc_1_bus_0[1]), .BUS_2(pc_1_bus_0[2]), .BUS_3(pc_1_bus_0[3]));
  MAR MAR (
    .A_3(MAR_a_3), .A_2(MAR_a_2), .A_1(MAR_a_1), .A_0(MAR_a_0), .BUS_0(pc_1_bus_0[0]), .BUS_1(pc_1_bus_0[1]),
    .BUS_2(pc_1_bus_0[2]), .BUS_3(pc_1_bus_0[3]), .DBG(MAR_dbg), .nMI(Controller_nmi),
    .nPROG(programmer_1_nprog), .CLR(CLR), .CLK(CLK_t), .PA_3(PADDR[3]), .PA_2(PADDR[2]), .PA_1(PADDR[1]),
    .PA_0(PADDR[0]));
  RAM ram_1 (
    .A3(MAR_a_3), .A2(MAR_a_2), .A1(MAR_a_1), .A0(MAR_a_0), .DBG({ram_1_dbg_2, ram_1_dbg}),
    .RI(Controller_ri), .nRO(Controller_nro), .nPROG(programmer_1_nprog), .PDATA(programmer_1_pdata),
    .nPULSE(programmer_1_npulse), .CLK(CLK_t), .BUS_0(pc_1_bus_0[0]), .BUS_1(pc_1_bus_0[1]),
    .BUS_2(pc_1_bus_0[2]), .BUS_3(pc_1_bus_0[3]), .BUS_4(ram_1_bus_7[0]), .BUS_5(ram_1_bus_7[1]),
    .BUS_6(ram_1_bus_7[2]), .BUS_7(ram_1_bus_7[3]));
  Out_Register Out_Register (
    .BUS_0(pc_1_bus_0[0]), .BUS_1(pc_1_bus_0[1]), .BUS_2(pc_1_bus_0[2]), .BUS_3(pc_1_bus_0[3]),
    .BUS_4(ram_1_bus_7[0]), .BUS_5(ram_1_bus_7[1]), .BUS_6(ram_1_bus_7[2]), .BUS_7(ram_1_bus_7[3]),
    .XCLK(clk_3), .nSEL(Out_Register_nsel), .A_P(Out_Register_a_p), .MODE(Signed), .OI(Controller_oi),
    .nCLR(nCLR), .CLK(CLK_t));
  Clock clock_1 (
    .DBG(clock_1_dbg), .CLK(CLK_t), .nCLK(nCLK), .XCLK(clk), .HLT(Controller_hlt), .nRUN(not_2_out),
    .STEP(Step_out));
  LED _7_2 (.in(ram_1_bus_7[3]));
  LED led_1 (.in(clock_1_dbg));
  LED _6_2 (.in(ram_1_bus_7[2]));
  LED _5_2 (.in(ram_1_bus_7[1]));
  LED _4_6 (.in(ram_1_bus_7[0]));
  LED _3_2 (.in(pc_1_bus_0[3]));
  LED _2_6 (.in(pc_1_bus_0[2]));
  LED _1_6 (.in(pc_1_bus_0[1]));
  LED _0_2 (.in(pc_1_bus_0[0]));
  Seven_Seg_Hex seven_seg_hex_5 (.d(ram_1_bus_7), .dp(1'b0));
  A_Register a_register_1 (
    .BUS_0(pc_1_bus_0[0]), .BUS_1(pc_1_bus_0[1]), .BUS_2(pc_1_bus_0[2]), .BUS_3(pc_1_bus_0[3]),
    .BUS_4(ram_1_bus_7[0]), .BUS_5(ram_1_bus_7[1]), .BUS_6(ram_1_bus_7[2]), .BUS_7(ram_1_bus_7[3]),
    .DBG({a_register_1_dbg_2, a_register_1_dbg}), .nAI(Controller_nai), .nAO(Controller_nao), .CLR(CLR),
    .CLK(CLK_t), .A_7(a_register_1_a_7), .A_6(a_register_1_a_6), .A_5(a_register_1_a_5),
    .A_4(a_register_1_a_4), .A_3(a_register_1_a_3), .A_2(a_register_1_a_2), .A_1(a_register_1_a_1),
    .A_0(a_register_1_a_0));
  ALU ALU (
    .DBG({ALU_dbg_3, ALU_dbg_2, ALU_dbg}), .CF(ALU_cf), .ZF(ALU_zf), .nEO(Controller_neo),
    .SU(Controller_su), .nFI(Controller_nfi), .CLR(CLR), .CLK(CLK_t), .B_7(b_register_1_b_7),
    .B_6(b_register_1_b_6), .B_5(b_register_1_b_5), .B_4(b_register_1_b_4), .B_3(b_register_1_b_3),
    .B_2(b_register_1_b_2), .B_1(b_register_1_b_1), .B_0(b_register_1_b_0), .A_7(a_register_1_a_7),
    .A_6(a_register_1_a_6), .A_5(a_register_1_a_5), .A_4(a_register_1_a_4), .A_3(a_register_1_a_3),
    .A_2(a_register_1_a_2), .A_1(a_register_1_a_1), .A_0(a_register_1_a_0), .BUS_0(pc_1_bus_0[0]),
    .BUS_1(pc_1_bus_0[1]), .BUS_2(pc_1_bus_0[2]), .BUS_3(pc_1_bus_0[3]), .BUS_4(ram_1_bus_7[0]),
    .BUS_5(ram_1_bus_7[1]), .BUS_6(ram_1_bus_7[2]), .BUS_7(ram_1_bus_7[3]));
  B_Register b_register_1 (
    .BUS_0(pc_1_bus_0[0]), .BUS_1(pc_1_bus_0[1]), .BUS_2(pc_1_bus_0[2]), .BUS_3(pc_1_bus_0[3]),
    .BUS_4(ram_1_bus_7[0]), .BUS_5(ram_1_bus_7[1]), .BUS_6(ram_1_bus_7[2]), .BUS_7(ram_1_bus_7[3]),
    .DBG({b_register_1_dbg_2, b_register_1_dbg}), .nBI(Controller_nbi), .nBO(1'b0), .CLR(CLR), .CLK(CLK_t),
    .B_7(b_register_1_b_7), .B_6(b_register_1_b_6), .B_5(b_register_1_b_5), .B_4(b_register_1_b_4),
    .B_3(b_register_1_b_3), .B_2(b_register_1_b_2), .B_1(b_register_1_b_1), .B_0(b_register_1_b_0));
  I_Register i_register_1 (
    .BUS_0(pc_1_bus_0[0]), .BUS_1(pc_1_bus_0[1]), .BUS_2(pc_1_bus_0[2]), .BUS_3(pc_1_bus_0[3]),
    .BUS_4(ram_1_bus_7[0]), .BUS_5(ram_1_bus_7[1]), .BUS_6(ram_1_bus_7[2]), .BUS_7(ram_1_bus_7[3]),
    .DBG({i_register_1_dbg_2, i_register_1_dbg}), .nII(Controller_nii), .nIO(Controller_nio), .CLR(CLR),
    .CLK(CLK_t), .IR_7(i_register_1_ir_7), .IR_6(i_register_1_ir_6), .IR_5(i_register_1_ir_5),
    .IR_4(i_register_1_ir_4));
  Ctrl Controller (
    .HLT(Controller_hlt), .OI(Controller_oi), .nRO(Controller_nro), .RI(Controller_ri), .nMI(Controller_nmi),
    .CE(Controller_ce), .nJ(Controller_nj), .nCO(Controller_nco), .DBGS(Controller_dbgs),
    .nIO(Controller_nio), .nII(Controller_nii), .nBI(Controller_nbi), .nFI(Controller_nfi),
    .SU(Controller_su), .nEO(Controller_neo), .ZF(ALU_zf), .CF(ALU_cf), .nAO(Controller_nao),
    .nAI(Controller_nai), .RESET(Reset_out), .CLR(CLR), .nCLR(nCLR), .nCLK(CLK_t), .DBGC(Controller_dbgc),
    .IR_7(i_register_1_ir_7), .IR_6(i_register_1_ir_6), .IR_5(i_register_1_ir_5), .IR_4(i_register_1_ir_4));
  Seven_Seg_Hex seven_seg_hex_6 (.d(pc_1_bus_0), .dp(1'b0));
  LED _7_3 (.in(a_register_1_dbg_2[3]));
  LED _7_4 (.in(ALU_dbg_2[3]));
  LED _7_5 (.in(b_register_1_dbg_2[3]));
  LED Inst_3 (.in(i_register_1_dbg_2[3]));
  LED T1 (.in(Controller_dbgs[7]));
  LED HLT (.in(Controller_dbgc[0]));
  LED _6_3 (.in(a_register_1_dbg_2[2]));
  LED _5_3 (.in(a_register_1_dbg_2[1]));
  LED _6_4 (.in(ALU_dbg_2[2]));
  LED _5_4 (.in(ALU_dbg_2[1]));
  LED _6_5 (.in(b_register_1_dbg_2[2]));
  LED _5_5 (.in(b_register_1_dbg_2[1]));
  LED Inst_2 (.in(i_register_1_dbg_2[2]));
  LED Inst_1 (.in(i_register_1_dbg_2[1]));
  LED T3 (.in(Controller_dbgs[5]));
  LED T2 (.in(Controller_dbgs[6]));
  LED MI (.in(Controller_dbgc[1]));
  LED RI (.in(Controller_dbgc[2]));
  LED _4_7 (.in(a_register_1_dbg_2[0]));
  LED _3_3 (.in(a_register_1_dbg[3]));
  LED _4_8 (.in(ALU_dbg_2[0]));
  LED _3_4 (.in(ALU_dbg[3]));
  LED _4_9 (.in(b_register_1_dbg_2[0]));
  LED _3_5 (.in(b_register_1_dbg[3]));
  LED Data_3 (.in(i_register_1_dbg[3]));
  LED Inst_0 (.in(i_register_1_dbg_2[0]));
  LED T5 (.in(Controller_dbgs[3]));
  LED T4 (.in(Controller_dbgs[4]));
  LED RO (.in(Controller_dbgc[3]));
  LED IO (.in(Controller_dbgc[4]));
  LED _2_7 (.in(a_register_1_dbg[2]));
  LED _1_7 (.in(a_register_1_dbg[1]));
  LED _2_8 (.in(ALU_dbg[2]));
  LED _1_8 (.in(ALU_dbg[1]));
  LED _2_9 (.in(b_register_1_dbg[2]));
  LED _1_9 (.in(b_register_1_dbg[1]));
  LED Data_2 (.in(i_register_1_dbg[2]));
  LED Data_1 (.in(i_register_1_dbg[1]));
  LED II (.in(Controller_dbgc[5]));
  LED AI (.in(Controller_dbgc[6]));
  Seven_Seg_Hex seven_seg_hex_7 (.d(a_register_1_dbg_2), .dp(1'b0));
  LED _0_3 (.in(a_register_1_dbg[0]));
  Seven_Seg_Hex seven_seg_hex_8 (.d(ALU_dbg_2), .dp(1'b0));
  LED _0_4 (.in(ALU_dbg[0]));
  Seven_Seg_Hex seven_seg_hex_9 (.d(b_register_1_dbg_2), .dp(1'b0));
  LED _0_5 (.in(b_register_1_dbg[0]));
  Seven_Seg_Hex seven_seg_hex_10 (.d(i_register_1_dbg_2), .dp(1'b0));
  LED Data_0 (.in(i_register_1_dbg[0]));
  LED EO (.in(Controller_dbgc[8]));
  LED AO (.in(Controller_dbgc[7]));
  Seven_Seg_Hex seven_seg_hex_11 (.d(a_register_1_dbg), .dp(1'b0));
  Seven_Seg_Hex seven_seg_hex_12 (.d(ALU_dbg), .dp(1'b0));
  Seven_Seg_Hex seven_seg_hex_13 (.d(b_register_1_dbg), .dp(1'b0));
  Seven_Seg_Hex seven_seg_hex_14 (.d(i_register_1_dbg), .dp(1'b0));
  LED BI (.in(Controller_dbgc[10]));
  LED SU (.in(Controller_dbgc[9]));
  Instr_Display instr_display (.INST({i_register_1_dbg_2, i_register_1_dbg}), .DISP(instr_display_disp));
  LED CE (.in(Controller_dbgc[12]));
  LED OI (.in(Controller_dbgc[11]));
  LED CF (.in(ALU_dbg_3[8]));
  LED ZF (.in(ALU_dbg_3[9]));
  LED J (.in(Controller_dbgc[14]));
  LED CO (.in(Controller_dbgc[13]));
  LED FI (.in(Controller_dbgc[15]));
  LED NOP (.in(instr_display_disp[0]));
  LED LDA (.in(instr_display_disp[1]));
  LED ADD (.in(instr_display_disp[2]));
  LED SUB (.in(instr_display_disp[3]));
  LED STA (.in(instr_display_disp[4]));
  LED LDI (.in(instr_display_disp[5]));
  LED JMP (.in(instr_display_disp[6]));
  LED JC (.in(instr_display_disp[7]));
  LED JZ (.in(instr_display_disp[8]));
  LED led_2 (.in(instr_display_disp[9]));
  LED led_3 (.in(instr_display_disp[10]));
  LED led_4 (.in(instr_display_disp[11]));
  LED led_5 (.in(instr_display_disp[12]));
  LED led_6 (.in(instr_display_disp[13]));
  LED OUT (.in(instr_display_disp[14]));
  LED HLT_2 (.in(instr_display_disp[15]));

  // Notes on the sheet:
  //   clk_2: Hz: 4
  //   clk_3: Hz: 4
  //   Addr
  //   Data
  //   PC
  //   MAR
  //   RAM
  //   Bus
  //   A Register
  //   Adder
  //   B Register
  //   Instr Register
  //   Step
  //   Control Bus
endmodule
