// Digital circuit Out-Register.dig as structural Verilog
module Out_Register (
  input  BUS_0,
  input  BUS_1,
  input  BUS_2,
  input  BUS_3,
  input  BUS_4,
  input  BUS_5,
  input  BUS_6,
  input  BUS_7,
  input  XCLK,
  input  MODE,
  input  nCLR,
  input  OI,
  input  CLK,
  output [3:0] nSEL,
  output [7:0] A_P
);

  wire _7476_1_p8, _7476_1_p14, _74173_1_p13, _74173_1_p14, _74173_1_p15, _74173_1_p16, _74173_2_p13,
       _74173_2_p14, _74173_2_p15, _74173_2_p16, CLR, nOI;

  not not_1 (nOI, OI);
  not not_2 (CLR, nCLR);
  // _74173 _74173_1: pin names not known; wires that end beside it: 1'b1, 1'b0, BUS_0, BUS_1, BUS_2, BUS_3, nOI, nOI, CLK, CLR, 1'b0, 1'b0, _74173_1_p13, _74173_1_p14, _74173_1_p15, _74173_1_p16
  // _74173 _74173_2: pin names not known; wires that end beside it: 1'b1, 1'b0, BUS_4, BUS_5, BUS_6, BUS_7, nOI, nOI, CLK, CLR, 1'b0, 1'b0, _74173_2_p13, _74173_2_p14, _74173_2_p15, _74173_2_p16
  // _7476 _7476_1: pin names not known; wires that end beside it: 1'b1, 1'b1, XCLK, 1'b1, 1'b1, 1'b1, 1'b1, _7476_1_p8, 1'b1, 1'b1, 1'b1, 1'b0, _7476_1_p8, _7476_1_p14
  ROM_Out rom_out_1 (
    .A_0(_74173_1_p13), .A_1(_74173_1_p14), .A_2(_74173_1_p15), .A_3(_74173_1_p16), .A_4(_74173_2_p13),
    .A_5(_74173_2_p14), .A_6(_74173_2_p15), .A_7(_74173_2_p16), .A_8(_7476_1_p8), .A_9(_7476_1_p14),
    .A_10(MODE), .nCE(1'b0), .D_0(A_P[0]), .D_1(A_P[1]), .D_2(A_P[2]), .D_3(A_P[3]), .D_4(A_P[4]),
    .D_5(A_P[5]), .D_6(A_P[6]), .D_7(A_P[7]));
  // _74139 _74139_1: pin names not known; wires that end beside it: 1'b0, _7476_1_p8, _7476_1_p14, 1'b0, 1'b0, 1'b0, 1'b1, 1'b0, nSEL[0], nSEL[1], nSEL[2], nSEL[3]

  // Other names for the same wires on the sheet: A = A_P[0]; B = A_P[1]; C = A_P[2]; D = A_P[3]; DP = A_P[7];
  //   E = A_P[4]; F = A_P[5]; G = A_P[6]; S1 = nSEL[0]; S2 = nSEL[1]; S3 = nSEL[2]; S4 = nSEL[3]

  // Notes on the sheet:
  //   nCLR: default 1
endmodule
