// Digital circuit PC.dig as structural Verilog
module PC (
  input  nCLR,
  input  CE,
  input  nJ,
  input  nCO,
  input  CLK,
  output BUS_3,
  output BUS_2,
  output BUS_1,
  output BUS_0,
  output [3:0] DBG
);

  // _74245 _74245_1: pin names not known; wires that end beside it: 1'b0, 1'b1, 1'b0, BUS_3, BUS_2, BUS_1, BUS_0, nCO, DBG[3], DBG[2], DBG[1], DBG[0]
  // _74161 _74161_1: pin names not known; wires that end beside it: DBG[3], DBG[2], DBG[1], DBG[0], 1'b0, 1'b1, BUS_3, BUS_2, BUS_1, BUS_0, CE, CE, CLK, nCLR, nJ

  // Notes on the sheet:
  //   nCLR: default 1
  //   nJ: default 1
  //   nCO: default 1
endmodule
