// Digital circuit Programmer.dig as structural Verilog
module Programmer (
  input  BCLK,
  input  [7:0] SDATA,
  input  [3:0] SADDR,
  input  nSPULSE,
  input  nSPROG,
  input  nLOAD,
  output nPULSE,
  output [7:0] PDATA,
  output nPROG,
  output [3:0] PADDR
);

  wire counter_1_ovf, nBPROG, nBPULSE, not_1_out, rs_ff_1_q;
  wire [3:0] BADDR;
  wire [7:0] BDATA;

  RS_FF rs_ff_1 (.S(~nLOAD), .C(BCLK), .R(counter_1_ovf), .Q(rs_ff_1_q), .nQ(nBPROG));
  Counter #(.Bits(4)) counter_1 (.en(rs_ff_1_q), .C(BCLK), .clr(counter_1_ovf), .out(BADDR), .ovf(counter_1_ovf));
  nor nor_1 (nPROG, ~nBPROG, ~nSPROG);  // NOr
  nand nand_1 (nBPULSE, rs_ff_1_q, not_1_out);
  not not_1 (not_1_out, BCLK);
  // _74157 _74157_1: pin names not known; wires that end beside it: nSPULSE, 1'b0, 1'b0, 1'b0, nBPULSE, 1'b0, 1'b0, 1'b0, nSPROG, 1'b0, 1'b1, 1'b0, nPULSE
  ROM #(.AddrBits(4), .isProgramMemory("true"), .Bits(8)) Bootstrap (.A(BADDR), .sel(1'b1), .D(BDATA));
  // _74157 _74157_2: pin names not known; wires that end beside it: SADDR[0], SADDR[1], SADDR[2], SADDR[3], BADDR[0], BADDR[1], BADDR[2], BADDR[3], nSPROG, 1'b0, 1'b1, 1'b0, PADDR[0], PADDR[1], PADDR[2], PADDR[3]
  // _74157 _74157_3: pin names not known; wires that end beside it: SDATA[0], SDATA[1], SDATA[2], SDATA[3], BDATA[0], BDATA[1], BDATA[2], BDATA[3], nSPROG, 1'b0, 1'b1, 1'b0, PDATA[0], PDATA[1], PDATA[2], PDATA[3]
  // _74157 _74157_4: pin names not known; wires that end beside it: SDATA[4], SDATA[5], SDATA[6], SDATA[7], BDATA[4], BDATA[5], BDATA[6], BDATA[7], nSPROG, 1'b0, 1'b1, 1'b0, PDATA[4], PDATA[5], PDATA[6], PDATA[7]

  // Notes on the sheet:
  //   BCLK: Hz: 2
  //   nPULSE: Program Pulse
  //   PDATA: Program Data
  //   SDATA: Switch Data
  //   SADDR: Switch Address -
  //   nSPULSE: Switch Address -, default 1
  //   nSPROG: Switch Program, default 1
  //   nPROG: Program Pulse
  //   PADDR: Program Address
  //   nLOAD: Switch Program, default 1
  //   contents of Bootstrap (hex, n*v repeats v):
  //   1e,2f,e0,f0,0,0,0,0,0,0,0,0,0,0,4,5
endmodule
