// Digital circuit RAM.dig as structural Verilog
module RAM (
  input  A3,
  input  A2,
  input  A1,
  input  A0,
  input  nPROG,
  input  nRO,
  input  RI,
  input  [7:0] PDATA,
  input  nPULSE,
  input  CLK,
  output [7:0] DBG,
  output BUS_7,
  output BUS_6,
  output BUS_5,
  output BUS_4,
  output BUS_3,
  output BUS_2,
  output BUS_1,
  output BUS_0
);

  wire _74157_1_p13, _74157_1_p14, _74157_1_p15, _74157_1_p16, _74157_3_p13, _74157_3_p14, _74157_3_p15,
       _74157_3_p16, _74189_1_p9, _74189_1_p13, _74189_1_p14, _74189_1_p15, _74189_1_p16, _74189_2_p13,
       _74189_2_p14, _74189_2_p15, _74189_2_p16, nand_1_out;

  // _74157 _74157_1: pin names not known; wires that end beside it: PDATA[7], PDATA[6], PDATA[5], PDATA[4], BUS_7, BUS_6, BUS_5, BUS_4, nPROG, 1'b0, 1'b1, 1'b0, _74157_1_p13, _74157_1_p14, _74157_1_p15, _74157_1_p16
  nand nand_1 (nand_1_out, RI, CLK);
  // _74189 _74189_1: pin names not known; wires that end beside it: A0, A1, A2, A3, _74157_1_p13, _74157_1_p14, _74157_1_p15, _74157_1_p16, _74189_1_p9, 1'b1, 1'b0, 1'b0, _74189_1_p13, _74189_1_p14, _74189_1_p15, _74189_1_p16
  PullUp pullup_1 (.out(nPULSE));
  // _74157 _74157_2: pin names not known; wires that end beside it: 1'b0, 1'b0, nPULSE, 1'b0, 1'b0, 1'b0, nand_1_out, 1'b0, nPROG, 1'b0, 1'b1, 1'b0, _74189_1_p9
  // _74157 _74157_3: pin names not known; wires that end beside it: PDATA[3], PDATA[2], PDATA[1], PDATA[0], BUS_3, BUS_2, BUS_1, BUS_0, nPROG, 1'b0, 1'b1, 1'b0, _74157_3_p13, _74157_3_p14, _74157_3_p15, _74157_3_p16
  // _74189 _74189_2: pin names not known; wires that end beside it: A0, A1, A2, A3, _74157_3_p13, _74157_3_p14, _74157_3_p15, _74157_3_p16, _74189_1_p9, 1'b1, 1'b0, 1'b0, _74189_2_p13, _74189_2_p14, _74189_2_p15, _74189_2_p16
  not not_1 (DBG[7], _74189_1_p13);
  not not_2 (DBG[6], _74189_1_p14);
  not not_3 (DBG[5], _74189_1_p15);
  not not_4 (DBG[4], _74189_1_p16);
  not not_5 (DBG[3], _74189_2_p13);
  not not_6 (DBG[2], _74189_2_p14);
  not not_7 (DBG[1], _74189_2_p15);
  not not_8 (DBG[0], _74189_2_p16);
  // _74245 _74245_1: pin names not known; wires that end beside it: 1'b1, 1'b1, 1'b0, DBG[7], DBG[6], DBG[5], DBG[4], DBG[3], DBG[2], DBG[1], DBG[0], nRO, BUS_7, BUS_6, BUS_5, BUS_4, BUS_3, BUS_2, BUS_1, BUS_0

  // Other names for the same wires on the sheet: PD_1 = PDATA[0]; PD_2 = PDATA[1]; PD_3 = PDATA[2]; PD_4 = PDATA[3];
  //   PD_5 = PDATA[4]; PD_6 = PDATA[5]; PD_7 = PDATA[6]; PD_8 = PDATA[7]; PROG = nPROG

  // Notes on the sheet:
  //   nPROG: default 1
  //   nRO: default 1
  //   nPULSE: default 1
endmodule
