// Digital circuit ROM-Out.dig as structural Verilog
module ROM_Out (
  input  A_0,
  input  A_1,
  input  A_2,
  input  A_3,
  input  A_4,
  input  A_5,
  input  A_6,
  input  A_7,
  input  A_8,
  input  A_9,
  input  A_10,
  input  nCE,
  output D_0,
  output D_1,
  output D_2,
  output D_3,
  output D_4,
  output D_5,
  output D_6,
  output D_7
);

  wire not_1_out;

  not not_1 (not_1_out, nCE);
  ROM #(.AddrBits(11), .Bits(8)) rom_1 (
    .A({A_10, A_9, A_8, A_7, A_6, A_5, A_4, A_3, A_2, A_1, A_0}), .sel(not_1_out),
    .D({D_7, D_6, D_5, D_4, D_3, D_2, D_1, D_0}));

  // Notes on the sheet:
  //   contents of rom_1 (hex, n*v repeats v):
  //   7e,30,6d,79,33,5b,5f,70,7f,7b,7e,30,6d,79,33,5b,5f,70,7f,7b,7e,30,6d,79,33,5b,5f,
  //   70,7f,7b,7e,30,6d,79,33,5b,5f,70,7f,7b,7e,30,6d,79,33,5b,5f,70,7f,7b,7e,30,6d,79,
  //   33,5b,5f,70,7f,7b,7e,30,6d,79,33,5b,5f,70,7f,7b,7e,30,6d,79,33,5b,5f,70,7f,7b,7e,
  //   30,6d,79,33,5b,5f,70,7f,7b,7e,30,6d,79,33,5b,5f,70,7f,7b,7e,30,6d,79,33,5b,5f,70,
  //   7f,7b,7e,30,6d,79,33,5b,5f,70,7f,7b,7e,30,6d,79,33,5b,5f,70,7f,7b,7e,30,6d,79,33,
  //   5b,5f,70,7f,7b,7e,30,6d,79,33,5b,5f,70,7f,7b,7e,30,6d,79,33,5b,5f,70,7f,7b,7e,30,
  //   6d,79,33,5b,5f,70,7f,7b,7e,30,6d,79,33,5b,5f,70,7f,7b,7e,30,6d,79,33,5b,5f,70,7f,
  //   7b,7e,30,6d,79,33,5b,5f,70,7f,7b,7e,30,6d,79,33,5b,5f,70,7f,7b,7e,30,6d,79,33,5b,
  //   5f,70,7f,7b,7e,30,6d,79,33,5b,5f,70,7f,7b,7e,30,6d,79,33,5b,5f,70,7f,7b,7e,30,6d,
  //   79,33,5b,5f,70,7f,7b,7e,30,6d,79,33,5b,7e,7e,7e,7e,7e,7e,7e,7e,7e,7e,30,30,30,30,
  //   30,30,30,30,30,30,6d,6d,6d,6d,6d,6d,6d,6d,6d,6d,79,79,79,79,79,79,79,79,79,79,33,
  //   33,33,33,33,33,33,33,33,33,5b,5b,5b,5b,5b,5b,5b,5b,5b,5b,5f,5f,5f,5f,5f,5f,5f,5f,
  //   5f,5f,70,70,70,70,70,70,70,70,70,70,7f,7f,7f,7f,7f,7f,7f,7f,7f,7f,7b,7b,7b,7b,7b,
  //   7b,7b,7b,7b,7b,7e,7e,7e,7e,7e,7e,7e,7e,7e,7e,30,30,30,30,30,30,30,30,30,30,6d,6d,
  //   6d,6d,6d,6d,6d,6d,6d,6d,79,79,79,79,79,79,79,79,79,79,33,33,33,33,33,33,33,33,33,
  //   33,5b,5b,5b,5b,5b,5b,5b,5b,5b,5b,5f,5f,5f,5f,5f,5f,5f,5f,5f,5f,70,70,70,70,70,70,
  //   70,70,70,70,7f,7f,7f,7f,7f,7f,7f,7f,7f,7f,7b,7b,7b,7b,7b,7b,7b,7b,7b,7b,7e,7e,7e,
  //   7e,7e,7e,7e,7e,7e,7e,30,30,30,30,30,30,30,30,30,30,6d,6d,6d,6d,6d,6d,6d,6d,6d,6d,
  //   79,79,79,79,79,79,79,79,79,79,33,33,33,33,33,33,33,33,33,33,5b,5b,5b,5b,5b,5b,7e,
  //   7e,7e,7e,7e,7e,7e,7e,7e,7e,7e,7e,7e,7e,7e,7e,7e,7e,7e,7e,7e,7e,7e,7e,7e,7e,7e,7e,
  //   7e,7e,7e,7e,7e,7e,7e,7e,7e,7e,7e,7e,7e,7e,7e,7e,7e,7e,7e,7e,7e,7e,7e,7e,7e,7e,7e,
  //   7e,7e,7e,7e,7e,7e,7e,7e,7e,7e,7e,7e,7e,7e,7e,7e,7e,7e,7e,7e,7e,7e,7e,7e,7e,7e,7e,
  //   7e,7e,7e,7e,7e,7e,7e,7e,7e,7e,7e,7e,7e,7e,7e,7e,7e,7e,30,30,30,30,30,30,30,30,30,
  //   30,30,30,30,30,30,30,30,30,30,30,30,30,30,30,30,30,30,30,30,30,30,30,30,30,30,30,
  //   30,30,30,30,30,30,30,30,30,30,30,30,30,30,30,30,30,30,30,30,30,30,30,30,30,30,30,
  //   30,30,30,30,30,30,30,30,30,30,30,30,30,30,30,30,30,30,30,30,30,30,30,30,30,30,30,
  //   30,30,30,30,30,30,30,30,30,30,6d,6d,6d,6d,6d,6d,6d,6d,6d,6d,6d,6d,6d,6d,6d,6d,6d,
  //   6d,6d,6d,6d,6d,6d,6d,6d,6d,6d,6d,6d,6d,6d,6d,6d,6d,6d,6d,6d,6d,6d,6d,6d,6d,6d,6d,
  //   6d,6d,6d,6d,6d,6d,6d,6d,6d,6d,6d,6d,0,0,0,0,0,0,0,0,0,0,0,0,0,0,0,0,0,0,0,0,0,0,0,
  //   0,0,0,0,0,0,0,0,0,0,0,0,0,0,0,0,0,0,0,0,0,0,0,0,0,0,0,0,0,0,0,0,0,0,0,0,0,0,0,0,0,
  //   0,0,0,0,0,0,0,0,0,0,0,0,0,0,0,0,0,0,0,0,0,0,0,0,0,0,0,0,0,0,0,0,0,0,0,0,0,0,0,0,0,
  //   0,0,0,0,0,0,0,0,0,0,0,0,0,0,0,0,0,0,0,0,0,0,0,0,0,0,0,0,0,0,0,0,0,0,0,0,0,0,0,0,0,
  //   0,0,0,0,0,0,0,0,0,0,0,0,0,0,0,0,0,0,0,0,0,0,0,0,0,0,0,0,0,0,0,0,0,0,0,0,0,0,0,0,0,
  //   0,0,0,0,0,0,0,0,0,0,0,0,0,0,0,0,0,0,0,0,0,0,0,0,0,0,0,0,0,0,0,0,0,0,0,0,0,0,0,0,0,
  //   0,0,0,0,0,0,0,0,0,0,0,0,0,0,0,0,0,0,0,0,0,0,0,0,0,0,0,0,7e,30,6d,79,33,5b,5f,70,7f,
  //   7b,7e,30,6d,79,33,5b,5f,70,7f,7b,7e,30,6d,79,33,5b,5f,70,7f,7b,7e,30,6d,79,33,5b,
  //   5f,70,7f,7b,7e,30,6d,79,33,5b,5f,70,7f,7b,7e,30,6d,79,33,5b,5f,70,7f,7b,7e,30,6d,
  //   79,33,5b,5f,70,7f,7b,7e,30,6d,79,33,5b,5f,70,7f,7b,7e,30,6d,79,33,5b,5f,70,7f,7b,
  //   7e,30,6d,79,33,5b,5f,70,7f,7b,7e,30,6d,79,33,5b,5f,70,7f,7b,7e,30,6d,79,33,5b,5f,
  //   70,7f,7b,7e,30,6d,79,33,5b,5f,70,7f,70,5f,5b,33,79,6d,30,7e,7b,7f,70,5f,5b,33,79,
  //   6d,30,7e,7b,7f,70,5f,5b,33,79,6d,30,7e,7b,7f,70,5f,5b,33,79,6d,30,7e,7b,7f,70,5f,
  //   5b,33,79,6d,30,7e,7b,7f,70,5f,5b,33,79,6d,30,7e,7b,7f,70,5f,5b,33,79,6d,30,7e,7b,
  //   7f,70,5f,5b,33,79,6d,30,7e,7b,7f,70,5f,5b,33,79,6d,30,7e,7b,7f,70,5f,5b,33,79,6d,
  //   30,7e,7b,7f,70,5f,5b,33,79,6d,30,7e,7b,7f,70,5f,5b,33,79,6d,30,7e,7b,7f,70,5f,5b,
  //   33,79,6d,30,7e,7e,7e,7e,7e,7e,7e,7e,7e,7e,30,30,30,30,30,30,30,30,30,30,6d,6d,6d,
  //   6d,6d,6d,6d,6d,6d,6d,79,79,79,79,79,79,79,79,79,79,33,33,33,33,33,33,33,33,33,33,
  //   5b,5b,5b,5b,5b,5b,5b,5b,5b,5b,5f,5f,5f,5f,5f,5f,5f,5f,5f,5f,70,70,70,70,70,70,70,
  //   70,70,70,7f,7f,7f,7f,7f,7f,7f,7f,7f,7f,7b,7b,7b,7b,7b,7b,7b,7b,7b,7b,7e,7e,7e,7e,
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endmodule
